# Fritzing sketch CPE301_Rank_Canon_Schematic (saved by Fritzing 0.9.10b)
breadboards: 1

parts:
  Arduino = Arduino Mega 2560 (Rev3)
  RTC = ZS-042 RTC Module
  Idle = smd LED [color="Green (560nm)" package="0603 [SMD]"]
  Disabled = smd LED [color="Yellow (585nm)" package="0603 [SMD]"]
  R2 = Resistor [tolerance=±5% resistance=330 package="2010 [SMD]"]
  R1 = Resistor [tolerance=±5% power=0.5W resistance=330 package=THT]
  Error = smd LED [color="Red (660nm)" package="0603 [SMD]"]
  R3 = Resistor [tolerance=±5% resistance=330 package="2010 [SMD]"]
  Running = smd LED [color="Blue (470nm)" package="0603 [SMD]"]
  R4 = Resistor [tolerance=±5% resistance=330 package="2010 [SMD]"]
  M1 = DC Motor [voltage_(max)=6V voltage_(min)=3V]
  Contrast_POT = POT [knob_status=50% power=0.5W package=pot_mammoth]
  Vent_Control_POT = POT [knob_status=50% power=0.5W package=pot_mammoth]
  LCD_Display = LCD-16X2 [package=lcd-16x2_noholes]
  Power_Module = Power plug
  State_Switch = Pushbutton [package="[THT]"]
  Error_Reset_Button = Pushbutton [package="[THT]"]
  Stepper_Motor = Stepper Motor - Unipolar
  TEMP/Humidity_Sensor = Humidity and Temperature Sensor RHT03
  Water_Level_Sensor_Place_Holder = Soil Moisture Sensor

nets:
  N1: Arduino.A8, LCD_Display.DB3
  N2: Arduino.A9, LCD_Display.DB4
  N3: Arduino.A10, LCD_Display.DB5
  N4: Arduino.A11, LCD_Display.DB6
  N5: Arduino.A12, LCD_Display.DB7
  N6: Arduino.A13, LCD_Display.A
  N7: Arduino.A14, LCD_Display.K
  N8: Arduino.A15, Water_Level_Sensor_Place_Holder.SIG
  N9: Arduino.A0, LCD_Display.VSS
  N10: Arduino.A1, LCD_Display.VDD
  N11: Arduino.A2, Vent_Control_POT.A
  N12: Arduino.A3, LCD_Display.RS
  N13: Arduino.A4, LCD_Display.R_W
  N14: Arduino.A5, LCD_Display.E
  N15: Arduino.A6, LCD_Display.DB0
  N16: Arduino.A7, LCD_Display.DB1
  N17: Arduino.D21/SCL, Arduino.SCL, RTC.SCL
  N18: Arduino.D20/SDA, RTC.SDA
  GND: Arduino.D18/TX1, Arduino.GND, Arduino.D2_PWM, RTC.GND, Contrast_POT.E, Vent_Control_POT.E, Power_Module.GND, State_Switch.Pin_3, State_Switch.Pin_4, Error_Reset_Button.Pin_3, Error_Reset_Button.Pin_4, TEMP/Humidity_Sensor.GND_2, Water_Level_Sensor_Place_Holder.GND
  N19: Arduino.D9_PWM, R1.Pin_0
  N20: Arduino.D8_PWM, R2.Pin_0
  N21: Arduino.D3_PWM, TEMP/Humidity_Sensor.Data-signal
  N22: Arduino.D4_PWM, M1.pin_2
  N23: Arduino.D6_PWM, R4.Pin_0
  N24: Arduino.D7_PWM, R3.Pin_0
  N25: Arduino.D34, Stepper_Motor.A
  N26: Arduino.D36, Stepper_Motor.C
  N27: Arduino.D38, Stepper_Motor.B
  N28: Arduino.D40, Stepper_Motor.D
  VCC: RTC.VCC, Idle.cathode, Disabled.cathode, Error.cathode, Running.cathode, M1.pin_1, Contrast_POT.S, Vent_Control_POT.S, Power_Module.VCC, Stepper_Motor.COMMON_2, TEMP/Humidity_Sensor.Vcc, Water_Level_Sensor_Place_Holder.VCC
  N29: Idle.anode, R1.Pin_1
  N30: Disabled.anode, R2.Pin_1
  N31: Error.anode, R3.Pin_1
  N32: Running.anode, R4.Pin_1
  N33: Contrast_POT.A, LCD_Display.VO
